// Logisim project ControlUnit.circ as structural Verilog: 14 circuits, main circuit main
module main (
  input  Clk,
  input  Reset,
  output [15:0] \output 
);

  wire alu_1_cf, alu_1_zf, and_1_out, CF_q, controlunit_1_alu_aa, controlunit_1_alu_cmp, controlunit_1_imm6,
       controlunit_1_imm9, controlunit_1_memread, controlunit_1_memwrite, controlunit_1_pcaddress,
       controlunit_1_pcwrite, controlunit_1_writee, or_1_out, ZF_q;
  wire [2:0] controlunit_1_reg1, controlunit_1_reg2, controlunit_1_write;
  wire [15:0] adder_1_out, adder_2_out, alu_1_output, controlled_buffer_1_out, multiplexer_1_out,
       multiplexer_2_out, multiplexer_3_out, multiplexer_4_out, n16_bitregister_1_output,
       n16_bitregister_2_output, pc_1_output, ram_1_data, registerfile_1_reg1_o, registerfile_1_reg2_o,
       signExtend6_output, signextend9_2_output, signExtend9_output, zeroExtend9_output;

  PC pc_1 (
    .\input (multiplexer_3_out), .Clk(Clk), .PcWrite(controlunit_1_pcwrite), .reset(Reset),
    .\output (pc_1_output));
  _16_BitRegister u_16_bitregister_1 (
    .Input(pc_1_output), .Output(n16_bitregister_1_output), .Clk(Clk), .Enable(1'b1), .Reset(Reset));
  and and_1 (and_1_out, Clk, controlunit_1_alu_cmp);
  D_FlipFLop ZF (.D(alu_1_zf), .Clock(and_1_out), .Reset(Reset), .Q(ZF_q));
  D_FlipFLop CF (.D(alu_1_cf), .Clock(and_1_out), .Reset(Reset), .Q(CF_q));
  signextend6 signExtend6 (.\input (\output ), .\output (signExtend6_output));
  signextend9 signExtend9 (.\input (\output ), .\output (signExtend9_output));
  ROM #(.addrWidth(16), .dataWidth(16)) rom_1 (.addr(n16_bitregister_1_output), .data(\output ), .sel(1'b1));
  Adder #(.width(16)) adder_1 (.a(n16_bitregister_1_output), .b(16'h1), .out(adder_1_out));  // open: cin, cout
  Multiplexer #(.width(16), .enable("false")) multiplexer_1 (
    .in0(registerfile_1_reg2_o), .in1(signExtend6_output), .out(multiplexer_1_out), .sel(controlunit_1_imm6));
  Multiplexer #(.width(16), .enable("false")) multiplexer_2 (
    .in0(multiplexer_1_out), .in1(signExtend9_output), .out(multiplexer_2_out), .sel(controlunit_1_imm9));
  signextend9 signextend9_2 (.\input (\output ), .\output (signextend9_2_output));
  Adder #(.width(16)) adder_2 (
    .a(signextend9_2_output), .b(n16_bitregister_1_output), .out(adder_2_out));  // open: cin, cout
  ControlUnit controlunit_1 (
    .Reg2(controlunit_1_reg2), .Reg1(controlunit_1_reg1), .Write(controlunit_1_write),
    .Instruction(\output ), .Clk(Clk), .Reset(Reset), .IMM6(controlunit_1_imm6), .IMM9(controlunit_1_imm9),
    .PCWrite(controlunit_1_pcwrite), .ZF(ZF_q), .CF(CF_q), .WriteE(controlunit_1_writee),
    .ALU_AA(controlunit_1_alu_aa), .ALU_Cmp(controlunit_1_alu_cmp), .MemRead(controlunit_1_memread),
    .MemWrite(controlunit_1_memwrite), .PCADDRESS(controlunit_1_pcaddress));
  RegisterFile registerfile_1 (
    .inputData(n16_bitregister_2_output), .Reg1_Input(controlunit_1_reg1), .Reg2_Input(controlunit_1_reg2),
    .Dst(controlunit_1_write), .writeEnable(controlunit_1_writee), .Reset(Reset), .Clk(Clk),
    .Reg1_O(registerfile_1_reg1_o), .Reg2_O(registerfile_1_reg2_o));
  Multiplexer #(.width(16)) multiplexer_3 (
    .in0(adder_1_out), .in1(adder_2_out), .out(multiplexer_3_out), .sel(controlunit_1_pcaddress),
    .en(controlunit_1_pcwrite));
  zeroextend9 zeroExtend9 (.\input (\output ), .\output (zeroExtend9_output));
  ALU alu_1 (
    .Input_1(registerfile_1_reg1_o), .Input_2(multiplexer_2_out), .ALU_aa(controlunit_1_alu_aa),
    .Output(alu_1_output), .CF(alu_1_cf), .ZF(alu_1_zf));
  assign controlled_buffer_1_out = or_1_out ? zeroExtend9_output : 16'bz;  // Controlled_Buffer controlled_buffer_1
  Multiplexer #(.width(16), .enable("false")) multiplexer_4 (
    .in0(alu_1_output), .in1(ram_1_data), .out(multiplexer_4_out), .sel(controlunit_1_memread));
  or or_1 (or_1_out, controlunit_1_memread, controlunit_1_memwrite);
  _16_BitRegister u_16_bitregister_2 (
    .Input(multiplexer_4_out), .Output(n16_bitregister_2_output), .Clk(Clk), .Enable(1'b1), .Reset(Reset));
  RAM #(.addrWidth(16), .dataWidth(16), .bus("separate")) ram_1 (
    .addr(controlled_buffer_1_out), .din(registerfile_1_reg1_o), .data(ram_1_data),
    .str(controlunit_1_memwrite), .sel(1'b1), .clk(Clk), .ld(controlunit_1_memread), .clr(1'b0));

  // Notes on the sheet:
  //   contents of rom_1 (hex, n*v repeats v):
  //   6000 6202 440 698 4680 9002 2808 3060 900c b008 a005 c008 d00c 4340 561f 440 e1ff
endmodule

module D_Latch (
  input  D1,
  input  Clock,
  input  Reset,
  output Q1
);

  wire and_1_out, and_2_out, nor_1_out, not_1_out;

  not not_1 (not_1_out, D1);
  and and_1 (and_1_out, D1, Clock);
  and and_2 (and_2_out, Clock, not_1_out);
  nor nor_1 (nor_1_out, and_1_out, Q1);
  nor nor_2 (Q1, nor_1_out, Reset, and_2_out);
endmodule

module D_FlipFLop (
  input  D,
  input  Clock,
  input  Reset,
  output Q
);

  wire d_latch_1_q1, not_1_out;

  not not_1 (not_1_out, Clock);
  D_Latch d_latch_1 (.D1(D), .Clock(not_1_out), .Reset(Reset), .Q1(d_latch_1_q1));
  D_Latch d_latch_2 (.D1(d_latch_1_q1), .Clock(Clock), .Reset(Reset), .Q1(Q));
endmodule

// RegisterF
module RegisterFile (
  input  [2:0] Reg1_Input,
  input  [2:0] Reg2_Input,
  input  [2:0] Dst,
  input  writeEnable,
  input  Clk,
  input  [15:0] inputData,
  input  Reset,
  output [15:0] Reg1_O,
  output [15:0] Reg2_O
);

  wire and_1_out, and_2_out, and_3_out, and_4_out, and_5_out, and_6_out, and_7_out, and_8_out,
       decoder_1_out0, decoder_1_out1, decoder_1_out2, decoder_1_out3, decoder_1_out4, decoder_1_out5,
       decoder_1_out6, decoder_1_out7, decoder_2_out0, decoder_2_out1, decoder_2_out2, decoder_2_out3,
       decoder_2_out4, decoder_2_out5, decoder_2_out6, decoder_2_out7, decoder_3_out0, decoder_3_out1,
       decoder_3_out2, decoder_3_out3, decoder_3_out4, decoder_3_out5, decoder_3_out6, decoder_3_out7;
  wire [15:0] n16_bitregister_1_output, n16_bitregister_2_output, n16_bitregister_3_output,
       n16_bitregister_4_output, n16_bitregister_5_output, n16_bitregister_6_output,
       n16_bitregister_7_output, n16_bitregister_8_output;

  Decoder #(.select(3), .enable("false")) decoder_1 (
    .out0(decoder_1_out0), .out1(decoder_1_out1), .out2(decoder_1_out2), .out3(decoder_1_out3),
    .out4(decoder_1_out4), .out5(decoder_1_out5), .out6(decoder_1_out6), .out7(decoder_1_out7),
    .sel(Reg1_Input));
  Decoder #(.select(3), .enable("false")) decoder_2 (
    .out0(decoder_2_out0), .out1(decoder_2_out1), .out2(decoder_2_out2), .out3(decoder_2_out3),
    .out4(decoder_2_out4), .out5(decoder_2_out5), .out6(decoder_2_out6), .out7(decoder_2_out7),
    .sel(Reg2_Input));
  Decoder #(.select(3), .enable("false")) decoder_3 (
    .out0(decoder_3_out0), .out1(decoder_3_out1), .out2(decoder_3_out2), .out3(decoder_3_out3),
    .out4(decoder_3_out4), .out5(decoder_3_out5), .out6(decoder_3_out6), .out7(decoder_3_out7), .sel(Dst));
  and and_1 (and_1_out, decoder_3_out0, writeEnable);
  and and_2 (and_2_out, decoder_3_out1, writeEnable);
  and and_3 (and_3_out, decoder_3_out2, writeEnable);
  and and_4 (and_4_out, decoder_3_out3, writeEnable);
  and and_5 (and_5_out, decoder_3_out4, writeEnable);
  and and_6 (and_6_out, decoder_3_out5, writeEnable);
  and and_7 (and_7_out, decoder_3_out6, writeEnable);
  and and_8 (and_8_out, decoder_3_out7, writeEnable);
  _16_BitRegister u_16_bitregister_1 (
    .Input(inputData), .Output(n16_bitregister_1_output), .Clk(Clk), .Enable(and_1_out), .Reset(Reset));
  _16_BitRegister u_16_bitregister_2 (
    .Input(inputData), .Output(n16_bitregister_2_output), .Clk(Clk), .Enable(and_2_out), .Reset(Reset));
  _16_BitRegister u_16_bitregister_3 (
    .Input(inputData), .Output(n16_bitregister_3_output), .Clk(Clk), .Enable(and_3_out), .Reset(Reset));
  _16_BitRegister u_16_bitregister_4 (
    .Input(inputData), .Output(n16_bitregister_4_output), .Clk(Clk), .Enable(and_4_out), .Reset(Reset));
  _16_BitRegister u_16_bitregister_5 (
    .Input(inputData), .Output(n16_bitregister_5_output), .Clk(Clk), .Enable(and_5_out), .Reset(Reset));
  _16_BitRegister u_16_bitregister_6 (
    .Input(inputData), .Output(n16_bitregister_6_output), .Clk(Clk), .Enable(and_6_out), .Reset(Reset));
  _16_BitRegister u_16_bitregister_7 (
    .Input(inputData), .Output(n16_bitregister_7_output), .Clk(Clk), .Enable(and_7_out), .Reset(Reset));
  _16_BitRegister u_16_bitregister_8 (
    .Input(inputData), .Output(n16_bitregister_8_output), .Clk(Clk), .Enable(and_8_out), .Reset(Reset));
  assign Reg1_O = decoder_1_out0 ? n16_bitregister_1_output : 16'bz;  // Controlled_Buffer controlled_buffer_1
  assign Reg2_O = decoder_2_out0 ? n16_bitregister_1_output : 16'bz;  // Controlled_Buffer controlled_buffer_2
  assign Reg1_O = decoder_1_out1 ? n16_bitregister_2_output : 16'bz;  // Controlled_Buffer controlled_buffer_3
  assign Reg2_O = decoder_2_out1 ? n16_bitregister_2_output : 16'bz;  // Controlled_Buffer controlled_buffer_4
  assign Reg1_O = decoder_1_out2 ? n16_bitregister_3_output : 16'bz;  // Controlled_Buffer controlled_buffer_5
  assign Reg2_O = decoder_2_out2 ? n16_bitregister_3_output : 16'bz;  // Controlled_Buffer controlled_buffer_6
  assign Reg1_O = decoder_1_out3 ? n16_bitregister_4_output : 16'bz;  // Controlled_Buffer controlled_buffer_7
  assign Reg2_O = decoder_2_out3 ? n16_bitregister_4_output : 16'bz;  // Controlled_Buffer controlled_buffer_8
  assign Reg1_O = decoder_1_out4 ? n16_bitregister_5_output : 16'bz;  // Controlled_Buffer controlled_buffer_9
  assign Reg2_O = decoder_2_out4 ? n16_bitregister_5_output : 16'bz;  // Controlled_Buffer controlled_buffer_10
  assign Reg1_O = decoder_1_out5 ? n16_bitregister_6_output : 16'bz;  // Controlled_Buffer controlled_buffer_11
  assign Reg2_O = decoder_2_out5 ? n16_bitregister_6_output : 16'bz;  // Controlled_Buffer controlled_buffer_12
  assign Reg1_O = decoder_1_out6 ? n16_bitregister_7_output : 16'bz;  // Controlled_Buffer controlled_buffer_13
  assign Reg2_O = decoder_2_out6 ? n16_bitregister_7_output : 16'bz;  // Controlled_Buffer controlled_buffer_14
  assign Reg1_O = decoder_1_out7 ? n16_bitregister_8_output : 16'bz;  // Controlled_Buffer controlled_buffer_15
  assign Reg2_O = decoder_2_out7 ? n16_bitregister_8_output : 16'bz;  // Controlled_Buffer controlled_buffer_16
endmodule

// ControlU
module ControlUnit (
  input  [15:0] Instruction,
  input  Clk,
  input  Reset,
  input  ZF,
  input  CF,
  output [2:0] Reg2,
  output WriteE,
  output [2:0] Reg1,
  output ALU_AA,
  output [2:0] Write,
  output ALU_Cmp,
  output MemRead,
  output MemWrite,
  output PCADDRESS,
  output PCWrite,
  output IMM6,
  output IMM9
);

  wire and_1_out, and_2_out, and_4_out, and_5_out, and_6_out, Count_3_out, Count_out, decoder_1_out0,
       decoder_1_out1, decoder_1_out3, decoder_1_out4, decoder_1_out5, decoder_1_out7, decoder_1_out8,
       decoder_1_out9, decoder_1_out11, decoder_1_out12, decoder_1_out13, decoder_1_out14, decoder_1_out15,
       not_1_out, not_2_out, not_3_out, not_4_out, not_5_out, not_6_out, not_7_out, not_8_out, not_9_out,
       not_10_out, not_11_out, not_12_out, not_13_out, not_14_out, not_15_out, not_16_out, not_17_out,
       not_18_out, not_19_out, not_20_out, not_21_out, not_22_out, or_2_out, or_3_out, PCWrite_out,
       Save_2_out, Save_3_out, Save_4_out, Save_5_out, Save_6_out, Save_out;
  wire [3:0] adder_1_out, controlled_buffer_5_out, count_2_out;

  not not_1 (not_1_out, Instruction[13]);
  not not_2 (not_2_out, Instruction[14]);
  not not_3 (not_3_out, Instruction[15]);
  not not_4 (not_4_out, Instruction[14]);
  not not_5 (not_5_out, Instruction[15]);
  not not_6 (not_6_out, Instruction[13]);
  not not_7 (not_7_out, Instruction[15]);
  not not_8 (not_8_out, Instruction[12]);
  assign Reg2 = not_9_out ? Instruction[5:3] : 3'bz;  // Controlled_Buffer controlled_buffer_1
  assign Reg1 = not_10_out ? Instruction[8:6] : 3'bz;  // Controlled_Buffer controlled_buffer_2
  and and_1 (and_1_out, Instruction[12], not_1_out, not_2_out, not_3_out);
  and and_2 (and_2_out, Instruction[12], Instruction[13], not_4_out, not_5_out);
  and and_3 (IMM9, Instruction[12], not_6_out, Instruction[14], not_7_out);
  and and_4 (and_4_out, not_8_out, Instruction[13], Instruction[14], Instruction[15]);
  or or_1 (IMM6, and_1_out, and_2_out);
  not not_9 (not_9_out, and_5_out);
  assign Reg2 = and_5_out ? Instruction[8:6] : 3'bz;  // Controlled_Buffer controlled_buffer_3
  assign Reg1 = or_2_out ? Instruction[11:9] : 3'bz;  // Controlled_Buffer controlled_buffer_4
  not not_10 (not_10_out, or_2_out);
  assign controlled_buffer_5_out = not_11_out ? Instruction[15:12] : 4'bz;  // Controlled_Buffer controlled_buffer_5
  not not_11 (not_11_out, Count_out);
  or Count (Count_out, and_1_out, and_2_out, IMM9, and_4_out);
  assign controlled_buffer_5_out = and_1_out ? 4'b0000 : 4'bz;  // Controlled_Buffer controlled_buffer_6
  assign controlled_buffer_5_out = and_2_out ? 4'b0010 : 4'bz;  // Controlled_Buffer controlled_buffer_7
  assign controlled_buffer_5_out = IMM9 ? 4'b0100 : 4'bz;  // Controlled_Buffer controlled_buffer_8
  assign controlled_buffer_5_out = and_4_out ? 4'b1001 : 4'bz;  // Controlled_Buffer controlled_buffer_9
  or or_2 (or_2_out, and_6_out, and_5_out);
  and and_5 (and_5_out, not_13_out, Instruction[14], not_12_out);
  not not_12 (not_12_out, Instruction[13]);
  not not_13 (not_13_out, Instruction[15]);
  and and_6 (and_6_out, Instruction[15], not_16_out, not_14_out, not_15_out);
  not not_14 (not_14_out, Instruction[13]);
  not not_15 (not_15_out, Instruction[12]);
  not not_16 (not_16_out, Instruction[14]);
  Adder #(.width(4)) adder_1 (.a(controlled_buffer_5_out), .b(4'b0010), .out(adder_1_out));  // open: cin, cout
  Count count_2 (
    .Clear(Save_out), .Load(decoder_1_out1), .\ıNPUT (adder_1_out), .Clk(Clk), .Count(Count_3_out),
    .Reset(Reset), .OUT(count_2_out));
  and Save (Save_out, PCWrite, not_17_out);
  not not_17 (not_17_out, Count_3_out);
  Decoder #(.select(4), .disabled(0), .enable("false")) decoder_1 (
    .out0(decoder_1_out0), .out1(decoder_1_out1), .out2(ALU_AA), .out3(decoder_1_out3),
    .out4(decoder_1_out4), .out5(decoder_1_out5), .out6(ALU_Cmp), .out7(decoder_1_out7),
    .out8(decoder_1_out8), .out9(decoder_1_out9), .out10(MemWrite), .out11(decoder_1_out11),
    .out12(decoder_1_out12), .out13(decoder_1_out13), .out14(decoder_1_out14), .out15(decoder_1_out15),
    .sel(count_2_out));
  or Count_3 (Count_3_out, decoder_1_out0, ALU_AA, decoder_1_out4, ALU_Cmp, decoder_1_out8);
  or u_PCWrite (PCWrite_out, decoder_1_out3, decoder_1_out5, decoder_1_out7, decoder_1_out9, MemWrite);
  or or_3 (or_3_out, decoder_1_out15, decoder_1_out14, decoder_1_out13, decoder_1_out12, decoder_1_out11);
  or or_4 (PCWrite, PCWrite_out, or_3_out);
  and Save_2 (Save_2_out, decoder_1_out11, ZF, not_18_out);
  not not_18 (not_18_out, CF);
  and Save_3 (Save_3_out, decoder_1_out12, not_19_out, not_20_out);
  not not_19 (not_19_out, ZF);
  not not_20 (not_20_out, CF);
  and Save_4 (Save_4_out, decoder_1_out13, not_21_out, CF);
  not not_21 (not_21_out, ZF);
  and Save_5 (Save_5_out, decoder_1_out14, not_22_out);
  not not_22 (not_22_out, CF);
  and Save_6 (Save_6_out, decoder_1_out15, ZF, CF);
  or or_5 (WriteE, decoder_1_out9, decoder_1_out5, decoder_1_out3);
  or or_6 (MemRead, decoder_1_out8, decoder_1_out9);
  or or_7 (PCADDRESS, Save_2_out, Save_3_out, Save_4_out, Save_5_out, Save_6_out, and_4_out);

  assign Write = Instruction[11:9];

  // Notes on the sheet:
  //   Jump
  //   Fetch1
  //   Fetch2
  //   Add1
  //   Add2
  //   And1
  //   And2
  //   Cmp1
  //   Cmp2
  //   Ld1
  //   Ld2
  //   St
  //   Je
  //   Ja
  //   Jb
  //   Jae
  //   Jbe
endmodule

module Count (
  input  Clear,
  input  Load,
  input  [3:0] \ıNPUT ,
  input  Clk,
  input  Count,
  input  Reset,
  output [3:0] OUT
);

  wire and_1_out, and_2_out, and_3_out, not_1_out, not_2_out, not_3_out, not_4_out, not_5_out, not_6_out,
       not_7_out, not_8_out, not_9_out, Save_out;
  wire [3:0] adder_1_out, controlled_buffer_1_out;

  not not_1 (not_1_out, Load);
  and and_1 (and_1_out, not_1_out, Clear, not_2_out);
  not not_2 (not_2_out, Count);
  not not_3 (not_3_out, Clear);
  and and_2 (and_2_out, not_3_out, Load, not_4_out);
  not not_4 (not_4_out, Count);
  not not_5 (not_5_out, Clear);
  and and_3 (and_3_out, not_5_out, not_6_out, Count);
  not not_6 (not_6_out, Load);
  assign controlled_buffer_1_out = and_1_out ? 4'b0000 : 4'bz;  // Controlled_Buffer controlled_buffer_1
  assign controlled_buffer_1_out = and_2_out ? \ıNPUT  : 4'bz;  // Controlled_Buffer controlled_buffer_2
  assign controlled_buffer_1_out = and_3_out ? adder_1_out : 4'bz;  // Controlled_Buffer controlled_buffer_3
  not not_7 (not_7_out, and_1_out);
  not not_8 (not_8_out, and_3_out);
  not not_9 (not_9_out, and_2_out);
  and Save (Save_out, not_7_out, not_9_out, not_8_out);
  assign controlled_buffer_1_out = Save_out ? OUT : 4'bz;  // Controlled_Buffer controlled_buffer_4
  _4_BitRegister u_4_bitregister_1 (.in_1(controlled_buffer_1_out), .Clk(Clk), .Reset(Reset), .Output(OUT));
  Adder #(.width(4)) adder_1 (.a(OUT), .b(4'b0001), .out(adder_1_out));  // open: cin, cout
endmodule

// CF
module _4_BitRegister (
  input  [3:0] in_1,
  input  Clk,
  input  Reset,
  output [3:0] Output
);

  D_FlipFLop d_flipflop_1 (.D(in_1[0]), .Clock(Clk), .Reset(Reset), .Q(Output[0]));
  D_FlipFLop d_flipflop_2 (.D(in_1[1]), .Clock(Clk), .Reset(Reset), .Q(Output[1]));
  D_FlipFLop d_flipflop_3 (.D(in_1[2]), .Clock(Clk), .Reset(Reset), .Q(Output[2]));
  D_FlipFLop d_flipflop_4 (.D(in_1[3]), .Clock(Clk), .Reset(Reset), .Q(Output[3]));
endmodule

module _16_BitRegister (
  input  [15:0] Input,
  input  Clk,
  input  Enable,
  input  Reset,
  output [15:0] Output
);

  wire and_1_out;

  and and_1 (and_1_out, Clk, Enable);
  D_FlipFLop d_flipflop_1 (.D(Input[15]), .Clock(and_1_out), .Reset(Reset), .Q(Output[15]));
  D_FlipFLop d_flipflop_2 (.D(Input[14]), .Clock(and_1_out), .Reset(Reset), .Q(Output[14]));
  D_FlipFLop d_flipflop_3 (.D(Input[13]), .Clock(and_1_out), .Reset(Reset), .Q(Output[13]));
  D_FlipFLop d_flipflop_4 (.D(Input[12]), .Clock(and_1_out), .Reset(Reset), .Q(Output[12]));
  D_FlipFLop d_flipflop_5 (.D(Input[10]), .Clock(and_1_out), .Reset(Reset), .Q(Output[10]));
  D_FlipFLop d_flipflop_6 (.D(Input[11]), .Clock(and_1_out), .Reset(Reset), .Q(Output[11]));
  D_FlipFLop d_flipflop_7 (.D(Input[9]), .Clock(and_1_out), .Reset(Reset), .Q(Output[9]));
  D_FlipFLop d_flipflop_8 (.D(Input[8]), .Clock(and_1_out), .Reset(Reset), .Q(Output[8]));
  D_FlipFLop d_flipflop_9 (.D(Input[7]), .Clock(and_1_out), .Reset(Reset), .Q(Output[7]));
  D_FlipFLop d_flipflop_10 (.D(Input[6]), .Clock(and_1_out), .Reset(Reset), .Q(Output[6]));
  D_FlipFLop d_flipflop_11 (.D(Input[5]), .Clock(and_1_out), .Reset(Reset), .Q(Output[5]));
  D_FlipFLop d_flipflop_12 (.D(Input[4]), .Clock(and_1_out), .Reset(Reset), .Q(Output[4]));
  D_FlipFLop d_flipflop_13 (.D(Input[3]), .Clock(and_1_out), .Reset(Reset), .Q(Output[3]));
  D_FlipFLop d_flipflop_14 (.D(Input[2]), .Clock(and_1_out), .Reset(Reset), .Q(Output[2]));
  D_FlipFLop d_flipflop_15 (.D(Input[1]), .Clock(and_1_out), .Reset(Reset), .Q(Output[1]));
  D_FlipFLop d_flipflop_16 (.D(Input[0]), .Clock(and_1_out), .Reset(Reset), .Q(Output[0]));
endmodule

module PC (
  input  [15:0] \input ,
  input  Clk,
  input  PcWrite,
  input  reset,
  output [15:0] \output 
);

  _16_BitRegister u_16_bitregister_1 (.Input(\input ), .Output(\output ), .Clk(Clk), .Enable(PcWrite), .Reset(reset));
endmodule

module signextend6 (
  input  [15:0] \input ,
  output [15:0] \output 
);


  assign \output  = {{11{\input [5]}}, \input [4:0]};
endmodule

module signextend9 (
  input  [15:0] \input ,
  output [15:0] \output 
);


  assign \output  = {{8{\input [8]}}, \input [7:0]};
endmodule

module oneextend6 (
  input  [15:0] \input ,
  output [15:0] \output 
);


  assign \output  = {{10{1'b1}}, \input [5:0]};
endmodule

module zeroextend9 (
  input  [15:0] \input ,
  output [15:0] \output 
);


  assign \output  = {{7{1'b0}}, \input [8:0]};
endmodule

module ALU (
  input  ALU_aa,
  input  [15:0] Input_1,
  input  [15:0] Input_2,
  output [15:0] Output,
  output CF,
  output ZF
);

  wire comparator_1_eq, comparator_1_gt, comparator_1_lt, not_1_out;
  wire [15:0] adder_1_out, and_1_out;

  assign Output = ALU_aa ? adder_1_out : 16'bz;  // Controlled_Buffer controlled_buffer_1
  Adder #(.width(16)) adder_1 (.a(Input_1), .b(Input_2), .out(adder_1_out));  // open: cin, cout
  not not_1 (not_1_out, ALU_aa);
  assign and_1_out = Input_2 & Input_1;  // AND_Gate and_1, 16 bits wide
  Comparator #(.width(16)) comparator_1 (
    .a(Input_1), .b(Input_2), .gt(comparator_1_gt), .eq(comparator_1_eq), .lt(comparator_1_lt));
  assign Output = not_1_out ? and_1_out : 16'bz;  // Controlled_Buffer controlled_buffer_2
  assign CF = comparator_1_eq ? 1'b0 : 1'bz;  // Controlled_Buffer controlled_buffer_3
  assign ZF = comparator_1_eq ? 1'b1 : 1'bz;  // Controlled_Buffer controlled_buffer_4
  assign CF = comparator_1_gt ? 1'b0 : 1'bz;  // Controlled_Buffer controlled_buffer_5
  assign ZF = comparator_1_gt ? 1'b0 : 1'bz;  // Controlled_Buffer controlled_buffer_6
  assign CF = comparator_1_lt ? 1'b1 : 1'bz;  // Controlled_Buffer controlled_buffer_7
  assign ZF = comparator_1_lt ? 1'b0 : 1'bz;  // Controlled_Buffer controlled_buffer_8
endmodule
